// Logisim project 8bitpc.circ as structural Verilog: 4 circuits, main circuit main
module main (
  input  Enable,
  input  in_2,
  input  in_3,
  input  in_4,
  input  in_5,
  input  in_6
);

  wire and_1_out, and_2_out, button_1_out, clock_1_out, or_1_out, Tick_out;
  wire [3:0] Address_q, octaltransciever_1_o1, Program_Counter_q;
  wire [7:0] Program_data;
  wire [7:4] octaltransciever_1_o5;

  Button button_1 (.out(button_1_out));
  Clock clock_1 (.out(clock_1_out));
  Button Tick (.out(Tick_out));
  Register #(.width(4)) Address (
    .D(octaltransciever_1_o1), .en(in_4), .clk(or_1_out), .Q(Address_q), .clr(button_1_out));
  and and_1 (and_1_out, clock_1_out, Enable);
  or or_1 (or_1_out, and_1_out, and_2_out);
  and and_2 (and_2_out, ~Enable, Tick_out);  // AND_Gate
  RAM #(.addrWidth(4), .trigger("high")) Program (.addr(Address_q), .we(1'b0), .oe(1'b1), .data(Program_data));
  LED led_1 (.in(or_1_out));
  Register Instruction (
    .D({octaltransciever_1_o5, octaltransciever_1_o1}), .en(in_2), .clk(or_1_out), .clr(button_1_out));  // open: Q
  OctalTransciever octaltransciever_1 (
    .O3(octaltransciever_1_o1[2]), .I8(Program_data[7]), .I4(Program_data[3]), .I3(Program_data[2]),
    .I7(Program_data[6]), .O2(octaltransciever_1_o1[1]), .I1(Program_data[0]), .O4(octaltransciever_1_o1[3]),
    .E(in_3), .I5(Program_data[4]), .I2(Program_data[1]), .I6(Program_data[5]),
    .O1(octaltransciever_1_o1[0]), .O5(octaltransciever_1_o5[4]), .O6(octaltransciever_1_o5[5]),
    .O7(octaltransciever_1_o5[6]), .O8(octaltransciever_1_o5[7]));
  Counter #(.width(4), .max('hf)) Program_Counter (
    .clr(button_1_out), .count(in_6), .clk(or_1_out), .Q(Program_Counter_q));  // open: load, up, D, carry
  QuadTransciever quadtransciever_1 (
    .O2(octaltransciever_1_o1[2]), .E(in_5), .I3(Program_Counter_q[1]), .I4(Program_Counter_q[0]),
    .O1(octaltransciever_1_o1[3]), .I2(Program_Counter_q[2]), .I1(Program_Counter_q[3]),
    .O3(octaltransciever_1_o1[1]), .O4(octaltransciever_1_o1[0]));
  // BCD_to_7_Segment_decoder bcd_to_7_segment_decoder_1: pin names not known
  _7_Segment_Display u_7_segment_display_1 ();  // open: g, f, a, b, e, d, c, dp
  // Binairy_to_BCD_converter #(.binvalue(4)) binairy_to_bcd_converter_1: pin names not known; wires that end beside it: Program_Counter_q
  _7_Segment_Display u_7_segment_display_2 ();  // open: g, f, a, b, e, d, c, dp
  // BCD_to_7_Segment_decoder bcd_to_7_segment_decoder_2: pin names not known
endmodule

module OctalTransciever (
  input  I1,
  input  I2,
  input  I3,
  input  I4,
  input  I5,
  input  I6,
  input  I7,
  input  I8,
  input  E,
  output O1,
  output O2,
  output O3,
  output O4,
  output O5,
  output O6,
  output O7,
  output O8
);

  assign O1 = E ? I1 : 1'bz;  // Controlled_Buffer controlled_buffer_1
  assign O2 = E ? I2 : 1'bz;  // Controlled_Buffer controlled_buffer_2
  assign O3 = E ? I3 : 1'bz;  // Controlled_Buffer controlled_buffer_3
  assign O4 = E ? I4 : 1'bz;  // Controlled_Buffer controlled_buffer_4
  assign O5 = E ? I5 : 1'bz;  // Controlled_Buffer controlled_buffer_5
  assign O6 = E ? I6 : 1'bz;  // Controlled_Buffer controlled_buffer_6
  assign O7 = E ? I7 : 1'bz;  // Controlled_Buffer controlled_buffer_7
  assign O8 = E ? I8 : 1'bz;  // Controlled_Buffer controlled_buffer_8
  Pull_Resistor pull_resistor_1 (.node(O1));
  Pull_Resistor pull_resistor_2 (.node(O2));
  Pull_Resistor pull_resistor_3 (.node(O3));
  Pull_Resistor pull_resistor_4 (.node(O4));
  Pull_Resistor pull_resistor_5 (.node(O5));
  Pull_Resistor pull_resistor_6 (.node(O6));
  Pull_Resistor pull_resistor_7 (.node(O7));
  Pull_Resistor pull_resistor_8 (.node(O8));

  // Notes on the sheet:
  //   O4: pull=down
  //   O2: pull=down
  //   I4: pull=down
  //   I7: pull=down
  //   I5: pull=down
  //   O7: pull=down
  //   I8: pull=down
  //   I2: pull=down
  //   I3: pull=down
  //   I1: pull=down
  //   O8: pull=down
  //   O5: pull=down
  //   O3: pull=down
  //   O6: pull=down
  //   I6: pull=down
  //   O1: pull=down
endmodule

module OctalBusTransciever (
  input  I,
  input  E,
  output O
);

  assign O = E ? I : 1'bz;  // Controlled_Buffer controlled_buffer_1
  Pull_Resistor pull_resistor_1 (.node(O));
endmodule

module QuadTransciever (
  input  I1,
  input  I2,
  input  I3,
  input  I4,
  input  E,
  output O1,
  output O2,
  output O3,
  output O4
);

  assign O1 = E ? I1 : 1'bz;  // Controlled_Buffer controlled_buffer_1
  assign O2 = E ? I2 : 1'bz;  // Controlled_Buffer controlled_buffer_2
  assign O3 = E ? I3 : 1'bz;  // Controlled_Buffer controlled_buffer_3
  assign O4 = E ? I4 : 1'bz;  // Controlled_Buffer controlled_buffer_4
  Pull_Resistor pull_resistor_1 (.node(O1));
  Pull_Resistor pull_resistor_2 (.node(O2));
  Pull_Resistor pull_resistor_3 (.node(O3));
  Pull_Resistor pull_resistor_4 (.node(O4));

  // Notes on the sheet:
  //   O1: pull=down
  //   I3: pull=down
  //   I2: pull=down
  //   O2: pull=down
  //   O4: pull=down
  //   I4: pull=down
  //   O3: pull=down
  //   I1: pull=down
endmodule
